// Logisim project Lab3Part1.circ as structural Verilog: 2 circuits, main circuit main
module main (
);

  wire alu_1_p5, alu_1_p6, alu_1_p7, alu_1_p8, CLK, not_1_out, T1_p6, T1CE, T1OE, T2CE, T2OE, WordR, WordW;
  wire [1:0] NS, register_1_q;
  wire [3:0] Addr, OPR;
  wire [31:0] Internal_Data_Bus, R, T1;
  wire [31:16] rom_1_data;

  Register #(.width(2)) register_1 (.D(NS), .Q(register_1_q), .clk(CLK));  // open: en, clr
  not not_1 (not_1_out, CLK);
  // Probe on {rom_1_data, OPR, Addr, WordR, WordW, T1CE, T1OE, T2CE, T2OE, NS}
  RAM #(.addrWidth(4), .dataWidth(32)) ram_1 (
    .addr(Addr), .data(Internal_Data_Bus), .clk(not_1_out), .ld(WordR));  // open: sel, clr
  ROM #(.addrWidth(2), .dataWidth(32)) rom_1 (
    .addr(register_1_q), .data({rom_1_data, OPR, Addr, WordR, WordW, T1CE, T1OE, T2CE, T2OE, NS}));  // open: sel
  T_Flip_Flop Clock (.Q(CLK));  // open: clk, T, Qn, preset, reset, en
  // ALU alu_1: pin names not known; wires that end beside it: T1, Internal_Data_Bus, OPR, R, alu_1_p5, alu_1_p6, alu_1_p7, alu_1_p8
  // Probe on alu_1_p5
  // Probe on alu_1_p6
  // Probe on alu_1_p7
  // Probe on alu_1_p8
  // Reg32 T1: pin names not known; wires that end beside it: CLK, Internal_Data_Bus, T1CE, T1OE, T1, T1_p6
  // Reg32 T2: pin names not known; wires that end beside it: CLK, R, T2CE, T2OE, Internal_Data_Bus, T1_p6
  Button button_1 (.out(T1_p6));

  // Notes on the sheet:
  //   contents of rom_1 (hex, n*v repeats v):
  //   ba1 299a 844
endmodule

module Part2 (
);

  wire alu_1_p5, alu_1_p6, alu_1_p7, alu_1_p8, and_1_out, ANOP, AOP, CLK, DW, FromDecode, not_1_out,
       not_2_out, not_3_out, OneSourceOP, SXW, SYW, T1_p6, T1CE, T1OE, T2CE, T2OE, WordR, WordW;
  wire [1:0] NS, register_2_q, SelectNS;
  wire [3:0] Addr, OPR;
  wire [15:0] register_1_q;
  wire [31:0] Internal_Data_Bus, R, T1;
  wire [31:13] rom_1_data;

  Register #(.width(16)) register_1 (.Q(register_1_q));  // open: D, en, clk, clr
  not not_1 (not_1_out, NS[1]);
  Register #(.width(2)) register_2 (.D(SelectNS), .Q(register_2_q), .clk(CLK));  // open: en, clr
  Multiplexer #(.width(2)) multiplexer_1 (.in0(NS), .in1(2'b10), .out(SelectNS), .sel(and_1_out));  // open: en
  and and_1 (and_1_out, OneSourceOP, FromDecode);
  and and_2 (FromDecode, not_1_out, NS[0]);
  not not_2 (not_2_out, register_1_q[15]);
  assign OPR = AOP ? register_1_q[15:12] : 4'bz;  // Controlled_Buffer AOP
  assign Addr = DW ? register_1_q[11:8] : 4'bz;  // Controlled_Buffer DW
  assign Addr = SXW ? register_1_q[7:4] : 4'bz;  // Controlled_Buffer SXW
  assign Addr = SYW ? register_1_q[3:0] : 4'bz;  // Controlled_Buffer SYW
  and and_3 (OneSourceOP, not_2_out, register_1_q[13], register_1_q[12]);
  ROM #(.addrWidth(2), .dataWidth(32)) rom_1 (
    .addr(register_2_q),
    .data({rom_1_data, AOP, ANOP, DW, SXW, SYW, WordR, WordW, T1CE, T1OE, T2CE, T2OE, NS}));  // open: sel
  T_Flip_Flop Clock (.Q(CLK));  // open: clk, T, Qn, preset, reset, en
  assign OPR = ANOP ? 4'b0000 : 4'bz;  // Controlled_Buffer ANOP
  not not_3 (not_3_out, CLK);
  RAM #(.addrWidth(4), .dataWidth(32)) ram_1 (
    .addr(Addr), .data(Internal_Data_Bus), .clk(not_3_out), .ld(WordR));  // open: sel, clr
  // Reg32 T1: pin names not known; wires that end beside it: CLK, Internal_Data_Bus, T1CE, T1OE, T1, T1_p6
  // Reg32 T2: pin names not known; wires that end beside it: CLK, R, T2CE, T2OE, Internal_Data_Bus, T1_p6
  Button button_1 (.out(T1_p6));
  // ALU alu_1: pin names not known; wires that end beside it: T1, Internal_Data_Bus, OPR, R, alu_1_p5, alu_1_p6, alu_1_p7, alu_1_p8
  // Probe on alu_1_p5
  // Probe on alu_1_p6
  // Probe on alu_1_p7
  // Probe on alu_1_p8

  // Notes on the sheet:
  //   contents of rom_1 (hex, n*v repeats v):
  //   801 aa2 119b c44
endmodule
