// Logisim project Lab4Part1.circ as structural Verilog: 2 circuits, main circuit main
module main (
);

  wire alu_1_p4, alu_1_p5, alu_1_p6, alu_1_p7, alu_1_p8, and_1_out, and_2_out, ANOP, AOP, Clock, CLR, DR,
       IBRead, IBWrite, Inverted_Clock, nor_1_out, or_1_out, reg32_1_p4, reg32_1_p6, reg32_2_p4, RegLD,
       RegSEL, SXR, SYR, T1CE, T1OE, T2CE, T2OE;
  wire [3:0] controlled_buffer_1_out, Opr;
  wire [7:0] Current_State_q, multiplexer_1_out, NextState, opcode, rom_1_data;
  wire [12:0] NotUsedInPart1;
  wire [23:0] Instruction_Register_q;
  wire [31:0] InterconnectionAddressBus, InterconnectionDataBus, InternalDataBus;

  // Probe on opcode
  Button Press_to_Clear_Internal_Processor_State (.out(CLR));
  and and_1 (and_1_out, Current_State_q[0], Current_State_q[1], ~Current_State_q[2], ~Current_State_q[3], ~Current_State_q[4], ~Current_State_q[5], ~Current_State_q[6], ~Current_State_q[7]);  // AND_Gate
  Register #(.width(32)) Instruction_Register (.Q({opcode, Instruction_Register_q}));  // open: D, en, clk, clr
  ROM rom_1 (.addr(opcode), .data(rom_1_data), .sel(and_1_out));
  Multiplexer #(.width(8)) multiplexer_1 (
    .in0(NextState), .in1(rom_1_data), .out(multiplexer_1_out), .sel(and_1_out));  // open: en
  // Probe on multiplexer_1_out
  // Probe on reg32_1_p4
  assign controlled_buffer_1_out = SYR ? Instruction_Register_q[15:12] : 4'bz;  // Controlled_Buffer controlled_buffer_1
  Register Current_State (.D(multiplexer_1_out), .Q(Current_State_q), .clk(Clock), .clr(CLR));  // open: en
  // Reg32 reg32_1: pin names not known; wires that end beside it: Clock, InternalDataBus, T1CE, reg32_1_p4, T1OE, reg32_1_p6, CLR
  assign controlled_buffer_1_out = SXR ? Instruction_Register_q[19:16] : 4'bz;  // Controlled_Buffer controlled_buffer_2
  // Probe on reg32_1_p6
  Clock Testing_clock (.out(Clock));
  assign controlled_buffer_1_out = DR ? Instruction_Register_q[23:20] : 4'bz;  // Controlled_Buffer controlled_buffer_3
  assign Opr = AOP ? opcode[3:0] : 4'bz;  // Controlled_Buffer controlled_buffer_4
  assign Opr = ANOP ? 4'b0000 : 4'bz;  // Controlled_Buffer controlled_buffer_5
  ROM #(.dataWidth(32)) rom_2 (
    .addr(Current_State_q),
    .data({NotUsedInPart1, AOP, ANOP, DR, SXR, SYR, RegSEL, RegLD, T1CE, T1OE, T2CE, T2OE, NextState}));  // open: sel
  not not_1 (Inverted_Clock, Clock);
  // Probe on NextState
  // Probe on InternalDataBus
  // ALU alu_1: pin names not known; wires that end beside it: reg32_1_p6, InternalDataBus, Opr, alu_1_p4, alu_1_p5, alu_1_p6, alu_1_p7, alu_1_p8
  LED led_1 (.in(alu_1_p5));
  LED led_2 (.in(alu_1_p6));
  LED led_3 (.in(alu_1_p7));
  LED led_4 (.in(alu_1_p8));
  // Probe on alu_1_p4
  // Probe on controlled_buffer_1_out
  // Probe on reg32_2_p4
  // Reg32 reg32_2: pin names not known; wires that end beside it: Clock, alu_1_p4, T2CE, reg32_2_p4, T2OE, InternalDataBus, CLR
  RAM #(.addrWidth(4), .dataWidth(32)) ram_1 (
    .addr(controlled_buffer_1_out), .data(InternalDataBus), .sel(RegSEL), .clk(Inverted_Clock), .ld(RegLD),
    .clr(CLR));
  // Probe on InternalDataBus
  nor nor_1 (nor_1_out, InterconnectionAddressBus[6], InterconnectionAddressBus[7], InterconnectionAddressBus[8], InterconnectionAddressBus[9], InterconnectionAddressBus[10], InterconnectionAddressBus[11], InterconnectionAddressBus[12], InterconnectionAddressBus[13], InterconnectionAddressBus[14], InterconnectionAddressBus[15], InterconnectionAddressBus[16], InterconnectionAddressBus[17], InterconnectionAddressBus[18], InterconnectionAddressBus[19], InterconnectionAddressBus[20], InterconnectionAddressBus[21], InterconnectionAddressBus[22], InterconnectionAddressBus[23], InterconnectionAddressBus[24], InterconnectionAddressBus[25], InterconnectionAddressBus[26], InterconnectionAddressBus[27], InterconnectionAddressBus[28], InterconnectionAddressBus[29], InterconnectionAddressBus[30], InterconnectionAddressBus[31]);
  and and_2 (and_2_out, nor_1_out, or_1_out);
  or or_1 (or_1_out, IBWrite, IBRead);
  RAM #(.addrWidth(6), .dataWidth(32)) ram_2 (
    .addr(InterconnectionAddressBus[5:0]), .data(InterconnectionDataBus), .sel(and_2_out),
    .clk(Inverted_Clock), .ld(IBRead));  // open: clr

  // Notes on the sheet:
  //   Decode ROM
  //   Use opcode to pick next state during decode state
  //   (Does not clear ROM contents)
  //   For each instruction, this ROM holds the next state that follows the Decode State.
  //   This design requies that Decode state is state  0x03
  //   contents of rom_1 (hex, n*v repeats v):
  //   0 4 4 5 4 4 4 5
  //   Control FSM
  //   upper 4 bits of opcode
  //   not used in this lab
  //   next state from Output ROM
  //   Control FSM Outputs
  //   (Poke to toggle)
  //   Invert for latching if needed
  //   contents of rom_2 (hex, n*v repeats v):
  //   20001 20002 20003 20007 2b805 47606 32100 7
  //   Register Address Bus
  //   16 x 32-bit Register Bank
  //   in Part 2 ONLY!
  //   Use this Main Memory component 
endmodule

module Part2 (
);

  wire AADD, alu_1_p4, alu_1_p5, alu_1_p6, alu_1_p7, alu_1_p8, and_1_out, and_2_out, ANOP, AOP, C1OE, Clock,
       CLR, DR, IBRead, IBWrite, Inverted_Clock, IRCE, MARCE, MAROE, MDRCE, MDRget, MDROE, MDRput, nor_1_out,
       or_1_out, PCOE, reg32_1_p4, reg32_1_p6, reg32_2_p4, RegLD, RegSEL, SXR, SYR, T1CE, T1OE, T2CE, T2OE;
  wire [3:0] controlled_buffer_2_out, Opr;
  wire [7:0] Current_State_q, multiplexer_1_out, NextState, opcode, rom_1_data;
  wire [23:0] Instruction_Register_q;
  wire [31:0] controlled_buffer_9_out, InterconnectionAddressBus, InterconnectionDataBus, InternalDataBus,
       MDR_p5;
  wire [31:31] rom_2_data;

  assign Opr = AADD ? 4'b0001 : 4'bz;  // Controlled_Buffer controlled_buffer_1
  // Probe on opcode
  Button Press_to_Clear_Internal_Processor_State (.out(CLR));
  and and_1 (and_1_out, Current_State_q[0], Current_State_q[1], ~Current_State_q[2], ~Current_State_q[3], ~Current_State_q[4], ~Current_State_q[5], ~Current_State_q[6], ~Current_State_q[7]);  // AND_Gate
  // Probe on reg32_1_p4
  Register #(.width(32)) Instruction_Register (
    .D(InternalDataBus), .en(IRCE), .Q({opcode, Instruction_Register_q}), .clk(Inverted_Clock));  // open: clr
  ROM rom_1 (.addr(opcode), .data(rom_1_data), .sel(and_1_out));
  // Reg32 reg32_1: pin names not known; wires that end beside it: Clock, InternalDataBus, T1CE, reg32_1_p4, T1OE, reg32_1_p6, CLR
  Multiplexer #(.width(8)) multiplexer_1 (
    .in0(NextState), .in1(rom_1_data), .out(multiplexer_1_out), .sel(and_1_out));  // open: en
  // Probe on multiplexer_1_out
  // Probe on reg32_1_p6
  assign controlled_buffer_2_out = SYR ? Instruction_Register_q[15:12] : 4'bz;  // Controlled_Buffer controlled_buffer_2
  Register Current_State (.D(multiplexer_1_out), .Q(Current_State_q), .clk(Clock), .clr(CLR));  // open: en
  assign controlled_buffer_2_out = SXR ? Instruction_Register_q[19:16] : 4'bz;  // Controlled_Buffer controlled_buffer_3
  assign InternalDataBus = C1OE ? 32'h1 : 32'bz;  // Controlled_Buffer controlled_buffer_4
  // ALU alu_1: pin names not known; wires that end beside it: reg32_1_p6, InternalDataBus, Opr, alu_1_p4, alu_1_p5, alu_1_p6, alu_1_p7, alu_1_p8
  LED led_1 (.in(alu_1_p5));
  LED led_2 (.in(alu_1_p6));
  LED led_3 (.in(alu_1_p7));
  LED led_4 (.in(alu_1_p8));
  Clock Testing_clock (.out(Clock));
  assign controlled_buffer_2_out = DR ? Instruction_Register_q[23:20] : 4'bz;  // Controlled_Buffer controlled_buffer_5
  assign Opr = AOP ? opcode[3:0] : 4'bz;  // Controlled_Buffer controlled_buffer_6
  assign Opr = ANOP ? 4'b0000 : 4'bz;  // Controlled_Buffer controlled_buffer_7
  ROM #(.dataWidth(32)) rom_2 (
    .addr(Current_State_q),
    .data({rom_2_data[31], IRCE, PCOE, C1OE, AADD, MARCE, MAROE, MDRCE, MDROE, MDRget, MDRput, IBRead, IBWrite, AOP, ANOP, DR, SXR, SYR, RegSEL, RegLD, T1CE, T1OE, T2CE, T2OE, NextState}));  // open: sel
  // Probe on InternalDataBus
  // Probe on alu_1_p4
  not not_1 (Inverted_Clock, Clock);
  assign controlled_buffer_2_out = PCOE ? 4'b1111 : 4'bz;  // Controlled_Buffer controlled_buffer_8
  // Probe on NextState
  // Probe on reg32_2_p4
  // Reg32 reg32_2: pin names not known; wires that end beside it: Clock, alu_1_p4, T2CE, reg32_2_p4, T2OE, InternalDataBus, CLR
  // Probe on controlled_buffer_2_out
  RAM #(.addrWidth(4), .dataWidth(32)) ram_1 (
    .addr(controlled_buffer_2_out), .data(InternalDataBus), .sel(RegSEL), .clk(Inverted_Clock), .ld(RegLD),
    .clr(CLR));
  // Probe on InternalDataBus
  assign controlled_buffer_9_out = MDRput ? InternalDataBus : 32'bz;  // Controlled_Buffer controlled_buffer_9
  assign InternalDataBus = MDRget ? MDR_p5 : 32'bz;  // Controlled_Buffer controlled_buffer_10
  // Reg32 MDR: pin names not known; wires that end beside it: Clock, controlled_buffer_9_out, MDRCE, MDROE, MDR_p5
  // Reg32 MAR: pin names not known; wires that end beside it: Clock, InternalDataBus, MARCE, MAROE, InterconnectionAddressBus
  assign controlled_buffer_9_out = IBRead ? InterconnectionDataBus : 32'bz;  // Controlled_Buffer controlled_buffer_11
  assign InterconnectionDataBus = IBWrite ? MDR_p5 : 32'bz;  // Controlled_Buffer controlled_buffer_12
  // Probe on InterconnectionAddressBus
  nor nor_1 (nor_1_out, InterconnectionAddressBus[6], InterconnectionAddressBus[7], InterconnectionAddressBus[8], InterconnectionAddressBus[9], InterconnectionAddressBus[10], InterconnectionAddressBus[11], InterconnectionAddressBus[12], InterconnectionAddressBus[13], InterconnectionAddressBus[14], InterconnectionAddressBus[15], InterconnectionAddressBus[16], InterconnectionAddressBus[17], InterconnectionAddressBus[18], InterconnectionAddressBus[19], InterconnectionAddressBus[20], InterconnectionAddressBus[21], InterconnectionAddressBus[22], InterconnectionAddressBus[23], InterconnectionAddressBus[24], InterconnectionAddressBus[25], InterconnectionAddressBus[26], InterconnectionAddressBus[27], InterconnectionAddressBus[28], InterconnectionAddressBus[29], InterconnectionAddressBus[30], InterconnectionAddressBus[31]);
  and and_2 (and_2_out, nor_1_out, or_1_out);
  or or_1 (or_1_out, IBWrite, IBRead);
  RAM #(.addrWidth(6), .dataWidth(32)) ram_2 (
    .addr(InterconnectionAddressBus[5:0]), .data(InterconnectionDataBus), .sel(and_2_out),
    .clk(Inverted_Clock), .ld(IBRead));  // open: clr

  // Notes on the sheet:
  //   Decode ROM
  //   Use opcode to pick next state during decode state
  //   ADD operation
  //   (Does not clear ROM contents)
  //   For each instruction, this ROM holds the next state that follows the Decode State.
  //   This design requies that Decode state is state  0x03
  //   contents of rom_1 (hex, n*v repeats v):
  //   0 4 4 5 4 4 4 5
  //   Control FSM
  //   upper 4 bits of opcode
  //   not used in this lab
  //   next state from Output ROM
  //   Control FSM Outputs
  //   (Poke to toggle)
  //   Invert for latching if needed
  //   contents of rom_2 (hex, n*v repeats v):
  //   24023801 1b100602 40c20003 20022107 2b805 47606 32100 7
  //   Register Address Bus
  //   16 x 32-bit Register Bank
  //   in Part 2 ONLY!
  //   Use this Main Memory component 
endmodule
